// Logisim project pipeline.circ as structural Verilog
module FetchUnit (
  input  [7:0] instrORimm,
  input  clk,
  input  reset,
  input  delayIN,
  input  stall,
  output [1:0] count,
  output [7:0] pipelineRegisters,
  output [7:0] pipeline,
  output delayOUT,
  output ready,
  output incPC,
  output [7:0] fetchReg
);

  wire and_1_out, nor_1_out, or_1_out, register_1_q;
  wire [7:0] multiplexer_1_out;

  Multiplexer #(.width(8)) multiplexer_1 (.in0({8{1'b0}}), .in1(instrORimm), .out(multiplexer_1_out), .sel(1'b1));
  // Probe on instrORimm
  // NoConnect on multiplexer_1_out[0]
  // NoConnect on multiplexer_1_out[1]
  // NoConnect on multiplexer_1_out[2]
  // NoConnect on multiplexer_1_out[3]
  // NoConnect on multiplexer_1_out[4]
  // NoConnect on multiplexer_1_out[5]
  Register #(.width(1)) register_1 (.D(nor_1_out), .en(1'b1), .clk(clk), .Q(register_1_q), .clr(reset));
  Register register_2 (.D(instrORimm), .en(1'b1), .clk(clk), .Q(fetchReg), .clr(reset));
  or or_1 (or_1_out, multiplexer_1_out[6], multiplexer_1_out[7]);
  and and_1 (and_1_out, or_1_out, nor_1_out);
  nor nor_1 (nor_1_out, count[0], count[1]);
  Counter #(.max('h3), .ongoal("stay"), .width(2)) counter_1 (
    .load(and_1_out), .D(multiplexer_1_out[7:6]), .count(1'b1), .Q(count), .up(1'b0), .clk(clk), .clr(reset));  // open: carry
  Demultiplexer #(.width(8)) demultiplexer_1 (
    .out0(pipelineRegisters), .out1(pipeline), .in(fetchReg), .sel(register_1_q));
  and and_2 (ready, register_1_q, 1'b1);

  assign delayOUT = 1'b1;
  assign incPC = 1'b1;

  // Notes on the sheet:
  //   Note: Ready signal is not meant for enabling the write input, it is to say all the
  //   immediate values are loaded into the pipeline registers to the decode units
  //   currently it is being used for write enable and must be changed in the future
endmodule

module delay (
  input  dIN,
  input  clock,
  input  reset,
  output dOUT,
  output ss
);

  wire d_ff_1_qn, d_ff_2_qn, undriven, undriven_2;

  D_Flip_Flop d_ff_1 (.D(dIN), .clk(clock), .Q(ss), .Qn(d_ff_1_qn), .preset(undriven), .reset(reset));
  // NoConnect on undriven
  D_Flip_Flop d_ff_2 (.D(ss), .clk(clock), .Q(dOUT), .Qn(d_ff_2_qn), .preset(undriven_2), .reset(reset));
  // NoConnect on d_ff_1_qn
  // NoConnect on undriven_2
  // NoConnect on d_ff_2_qn
endmodule

module test2 (
  input  load,
  input  [15:0] FFFFin,
  input  rst
);

  wire clk_out, decodeunit_1_alumode, decodeunit_1_cin, decodeunit_1_dload, decodeunit_1_dstore,
       decodeunit_1_enalu, decodeunit_1_regatodbus, fetchunit_1_delayout, fetchunit_1_incpc,
       fetchunit_1_ready;
  wire [1:0] fetchunit_1_count;
  wire [3:0] decodeunit_1_operation, decodeunit_1_rega, decodeunit_1_regb, decodeunit_1_regres;
  wire [7:0] alu_1_p6, dataMemory_dout, fetchunit_1_fetchreg, fetchunit_1_pipeline,
       fetchunit_1_pipelineregisters, generalpurposeregisters_1_a, generalpurposeregisters_1_b,
       instructionMemory_data, register_1_q, register_2_q, register_3_q;
  wire [15:0] decodeunit_1_dataaddr, programcounter_1_ffffout;

  ROM #(.addrWidth(16)) instructionMemory (.addr(programcounter_1_ffffout), .data(instructionMemory_data));
  ProgramCounter programcounter_1 (
    .FFFFin(FFFFin), .enable(fetchunit_1_incpc), .load(load), .clock(clk_out), .reset(rst),
    .FFFFout(programcounter_1_ffffout));
  // Probe on instructionMemory_data
  // Probe on fetchunit_1_fetchreg
  // Probe on fetchunit_1_count
  FetchUnit fetchunit_1 (
    .instrORimm(instructionMemory_data), .clk(rst), .reset(rst), .count(fetchunit_1_count),
    .pipelineRegisters(fetchunit_1_pipelineregisters), .pipeline(fetchunit_1_pipeline),
    .delayOUT(fetchunit_1_delayout), .ready(fetchunit_1_ready), .incPC(fetchunit_1_incpc),
    .fetchReg(fetchunit_1_fetchreg));  // open: delayIN, stall
  Register register_1 (
    .D(fetchunit_1_pipelineregisters), .en(fetchunit_1_delayout), .clk(rst), .Q(register_1_q), .clr(rst));
  Register register_2 (.D(register_1_q), .en(fetchunit_1_delayout), .clk(rst), .Q(register_2_q), .clr(rst));
  Register register_3 (.D(register_2_q), .en(fetchunit_1_delayout), .clk(rst), .Q(register_3_q), .clr(rst));
  RAM #(.addrWidth(16)) dataMemory (
    .addr(decodeunit_1_dataaddr), .we(decodeunit_1_dstore), .oe(decodeunit_1_dload), .clk(rst),
    .din(dataMemory_dout), .dout(dataMemory_dout));
  Clock clk (.out(clk_out));
  decodeUnit decodeunit_1 (
    .pipelineReg1(register_1_q), .pipelineReg2(register_2_q), .pipelineReg3(register_3_q),
    .pipelineIn(fetchunit_1_pipeline), .readyIN(fetchunit_1_ready), .clk(rst), .rst(rst),
    .dataaddr(decodeunit_1_dataaddr), .regAtoDBus(decodeunit_1_regatodbus), .regA(decodeunit_1_rega),
    .regB(decodeunit_1_regb), .operation(decodeunit_1_operation), .regRes(decodeunit_1_regres),
    .ALUmode(decodeunit_1_alumode), .Cin(decodeunit_1_cin), .enALU(decodeunit_1_enalu),
    .dload(decodeunit_1_dload), .dstore(decodeunit_1_dstore));  // open: databus, instraddr, pipelineOut, readyOUT
  assign dataMemory_dout = decodeunit_1_regatodbus ? generalpurposeregisters_1_a : 8'bz;  // Controlled_Buffer controlled_buffer_1
  // Probe on dataMemory_dout
  // Probe on dataMemory_dout
  // NoConnect on decodeunit_1_rega[3]
  // NoConnect on decodeunit_1_regb[3]
  // NoConnect on decodeunit_1_regres[3]
  // Probe on generalpurposeregisters_1_a
  GeneralPurposeRegisters generalpurposeregisters_1 (
    .write_Addr(decodeunit_1_regres[2:0]), .A_addr(decodeunit_1_rega[2:0]), .reset(rst), .clock(rst),
    .B_addr(decodeunit_1_regb[2:0]), .data(dataMemory_dout), .A(generalpurposeregisters_1_a),
    .B(generalpurposeregisters_1_b));
  // Probe on generalpurposeregisters_1_b
  assign dataMemory_dout = decodeunit_1_enalu ? alu_1_p6 : 8'bz;  // Controlled_Buffer controlled_buffer_2
  // ALU alu_1: pin names not known; wires that end beside it: decodeunit_1_alumode, decodeunit_1_operation, generalpurposeregisters_1_a, generalpurposeregisters_1_b, decodeunit_1_cin, alu_1_p6
  // NoConnect on dataMemory_dout

  // Notes on the sheet:
  //   contents of instructionMemory (hex, n*v repeats v):
  //   de 0 0 1 de 1 0 2 de 2 0 3 de 3 0 4 de 4 0 5 de 5 0 6 82 32 1 82 24 2 82 32 5
  //   PIPELINE REGISTERS 
  //   <= dataBus 
endmodule

module test1 (
  input  [7:0] instrORimm,
  input  clk,
  input  reset,
  input  delayIn,
  input  insertNOPE,
  output [7:0] PipelineRegisters,
  output [7:0] nextStage,
  output ready,
  output incPC
);

  wire and_1_out, and_2_out, c, or_1_out, or_2_out, register_1_q, t_ff_1_q, t_ff_1_qn;
  wire [1:0] counter_1_q;
  wire [7:0] demultiplexer_1_out0, demultiplexer_1_out1, multiplexer_1_out, register_2_q, register_3_q,
       register_4_q, register_5_q, register_6_q;

  Multiplexer #(.width(8)) multiplexer_1 (.in0({8{1'b0}}), .in1(instrORimm), .out(multiplexer_1_out), .sel(delayIn));
  // NoConnect on multiplexer_1_out[0]
  // NoConnect on multiplexer_1_out[1]
  // NoConnect on multiplexer_1_out[2]
  // NoConnect on multiplexer_1_out[3]
  // NoConnect on multiplexer_1_out[4]
  // NoConnect on multiplexer_1_out[5]
  Register #(.width(1)) register_1 (.D(c), .en(delayIn), .clk(clk), .Q(register_1_q), .clr(reset));
  or or_1 (or_1_out, delayIn, c);
  // NOT_Gate not_1 has open pins: in=insertNOPE, out=open
  or or_2 (or_2_out, multiplexer_1_out[6], multiplexer_1_out[7]);
  and and_1 (and_1_out, or_2_out, c);
  nor nor_1 (c, counter_1_q[0], counter_1_q[1]);
  Register register_2 (.D(instrORimm), .en(delayIn), .clk(clk), .Q(register_2_q), .clr(reset));
  // NOT_Gate not_2 has open pins: in=t_ff_1_q, out=open
  T_Flip_Flop t_ff_1 (.T(or_1_out), .clk(clk), .Q(t_ff_1_q), .Qn(t_ff_1_qn), .reset(reset), .preset(1'b0));
  // NoConnect on t_ff_1_qn
  Counter #(.max('h3), .ongoal("stay"), .width(2)) counter_1 (
    .load(and_1_out), .D(multiplexer_1_out[7:6]), .count(delayIn), .Q(counter_1_q), .up(1'b0), .clk(clk),
    .clr(reset));  // open: carry
  Demultiplexer #(.width(8)) demultiplexer_1 (
    .out0(demultiplexer_1_out0), .out1(demultiplexer_1_out1), .in(register_2_q), .sel(register_1_q));
  and and_2 (and_2_out, register_1_q, delayIn);
  Register register_3 (.D(demultiplexer_1_out0), .en(delayIn), .clk(clk), .Q(register_3_q), .clr(reset));
  Register register_4 (.D(demultiplexer_1_out1), .en(and_2_out), .clk(clk), .Q(register_4_q), .clr(reset));
  Register register_5 (.D(register_3_q), .en(delayIn), .clk(clk), .Q(register_5_q), .clr(reset));
  Register register_6 (.D(register_4_q), .en(and_2_out), .clk(clk), .Q(register_6_q), .clr(reset));
  Register register_7 (.D(register_5_q), .en(delayIn), .clk(clk), .Q(PipelineRegisters), .clr(reset));
  Register register_8 (.D(register_6_q), .en(and_2_out), .clk(clk), .Q(nextStage), .clr(reset));

  // Notes on the sheet:
  //   delay is used for requesting the pipeline to halt the next cycle 
  //   and it is not meant for handling pipeline hazards
endmodule

module decodeUnit (
  input  [7:0] pipelineReg1,
  input  [7:0] pipelineReg2,
  input  [7:0] pipelineReg3,
  input  [7:0] pipelineIn,
  input  readyIN,
  input  clk,
  input  rst,
  output [7:0] databus,
  output [15:0] instraddr,
  output [15:0] dataaddr,
  output regAtoDBus,
  output [3:0] regA,
  output [3:0] regB,
  output [3:0] operation,
  output [3:0] regRes,
  output [7:0] pipelineOut,
  output readyOUT,
  output ALUmode,
  output Cin,
  output enALU,
  output dload,
  output dstore
);

  wire [2:0] rom_1_data;
  wire [15:0] rom_2_data;
  wire [15:3] rom_1_data_2;
  wire [15:5] multiplexer_1_out;

  Register register_1 (.D(pipelineIn), .en(readyIN), .clk(clk), .Q(pipelineOut), .clr(rst));
  // NoConnect on pipelineOut[7]
  // NoConnect on pipelineOut[6]
  ROM #(.addrWidth(6), .dataWidth(16)) rom_1 (.addr(pipelineOut[5:0]), .data({rom_1_data_2, rom_1_data}));
  ROM #(.addrWidth(6), .dataWidth(16)) rom_2 (.addr(pipelineOut[5:0]), .data(rom_2_data));
  // NoConnect on rom_1_data_2[3]
  // NoConnect on rom_1_data_2[4]
  // NoConnect on rom_1_data_2[5]
  // NoConnect on rom_1_data_2[6]
  // NoConnect on rom_1_data_2[7]
  // NoConnect on rom_1_data_2[8]
  // NoConnect on rom_1_data_2[9]
  // NoConnect on rom_1_data_2[10]
  // NoConnect on rom_1_data_2[11]
  // NoConnect on rom_1_data_2[12]
  // NoConnect on rom_1_data_2[13]
  // NoConnect on rom_1_data_2[14]
  // NoConnect on rom_1_data_2[15]
  Multiplexer #(.width(16)) multiplexer_1 (
    .in0({16{1'b0}}), .in1(rom_2_data), .out({multiplexer_1_out, dstore, dload, enALU, Cin, ALUmode}),
    .sel(readyIN));
  pipelineRegFormatSelector pipelineregformatselector_1 (
    .pipelineReg1(pipelineReg1), .pipelineReg2(pipelineReg2), .pipelineReg3(pipelineReg3),
    .modeselect(rom_1_data), .dataBus(databus), .instrAddrBus(instraddr), .dataAddrBus(dataaddr),
    .enRegAtoDBus(regAtoDBus), .regRes(regRes), .operation(operation), .regA(regB), .regB(regA));
  // NoConnect on multiplexer_1_out[5]
  // NoConnect on multiplexer_1_out[6]
  // NoConnect on multiplexer_1_out[7]
  // NoConnect on multiplexer_1_out[8]
  // NoConnect on multiplexer_1_out[9]
  // NoConnect on multiplexer_1_out[10]
  // NoConnect on multiplexer_1_out[11]
  // NoConnect on multiplexer_1_out[12]
  // NoConnect on multiplexer_1_out[13]
  // NoConnect on multiplexer_1_out[14]
  // NoConnect on multiplexer_1_out[15]

  assign readyOUT = readyIN;

  // Notes on the sheet:
  //   Note: implement Ready signal it is not just a write enable signal it must only decode and execute instruction when on
endmodule

module pipelineRegFormatSelector (
  input  [7:0] pipelineReg1,
  input  [7:0] pipelineReg2,
  input  [7:0] pipelineReg3,
  input  [2:0] modeselect,
  output [7:0] dataBus,
  output [15:0] instrAddrBus,
  output [15:0] dataAddrBus,
  output enRegAtoDBus,
  output [3:0] regRes,
  output [3:0] operation,
  output [3:0] regA,
  output [3:0] regB
);

  wire decoder_1_out0, or_1_out;

  // NoConnect on dataBus
  // NoConnect on instrAddrBus
  // NoConnect on dataAddrBus
  assign dataAddrBus = enRegAtoDBus ? {pipelineReg2, pipelineReg3} : 16'bz;  // Controlled_Buffer controlled_buffer_1
  Decoder #(.enable("false"), .select(3)) decoder_1 (
    .out0(decoder_1_out0), .out1(enRegAtoDBus), .sel(modeselect));  // open: out2, out3, out4, out5, out6, out7
  or or_1 (or_1_out, enRegAtoDBus, decoder_1_out0);
  assign {operation, regRes} = or_1_out ? pipelineReg1 : 8'bz;  // Controlled_Buffer controlled_buffer_2
  assign {regB, regA} = decoder_1_out0 ? pipelineReg2 : 8'bz;  // Controlled_Buffer controlled_buffer_3
endmodule
